# Fritzing sketch Project Sketch (saved by Fritzing 0.9.3b)
stripboards: 1

parts:
  Part1 = Arduino Nano (Rev3.0) (ICSP)
  J7 = Basic Servo
  J1 = Basic Servo
  J4 = Basic Servo
  J5 = Basic Servo
  J3 = Basic Servo
  J6 = Basic Servo
  Part2 = Solar Cell  # not connected

nets:
  N1: Part1.D2, J3.pulse
  N2: Part1.D3, J1.pulse
  N3: Part1.D4, J7.pulse
  N4: Part1.D5, J6.pulse
  N5: Part1.D6, J5.pulse
  N6: Part1.D7, J4.pulse
  GND: Part1.GND, J7.gnd, J1.gnd, J4.gnd, J5.gnd, J3.gnd, J6.gnd
  VCC: Part1.5V, J1.vcc, J4.vcc, J5.vcc, J3.vcc, J6.vcc
