# Fritzing sketch Solar - step up - battery charger (saved by Fritzing 0.9.3b)

parts:
  Part1 = Solar Cell
  U1 = LM2596 step down module
  Mod1 = 3S-BMS
  BAT1 = 18650 battery holder [package=battery-18650-kit]
  BAT2 = 18650 battery holder [package=battery-18650-kit]
  BAT3 = 18650 battery holder [package=battery-18650-kit]

nets:
  N1: Part1.+, U1.IN+
  N2: Part1.-, U1.IN-, U1.OUT-, Mod1.-
  N3: U1.OUT+, Mod1.+
  N4: Mod1.0V, BAT3.-
  N5: Mod1.4.2V, BAT2.-, BAT3.+
  N6: Mod1.8.4V, BAT1.-, BAT2.+
  N7: Mod1.12.6V, BAT1.+

custom parts:
  LM2596 step down module: LM2596 DC-DC step down power supply module 3 A.
  3S-BMS: 3S-BMS LIPO battery charger / protection unit. Note pcb does not match the board as it will likely connect with wires, so pcb is 6 pads suitable for .1in header pins.
  18650 battery holder: 18650 Battery Holder
